# Fritzing sketch roomi (saved by Fritzing 0.9.3b)
breadboards: 1

parts:
  Q1 = Basic FET N-Channel [package="D2Pak [SMD]"]
  Raspberry_Pi_1 = Raspberry Pi 3 [part_number=RPI-3-V1.2]
  L1 = Solenoid
  D1 = Rectifier Diode [part_number=1N4001 package="300 mil [THT]"]
  R1 = Resistor [tolerance=±5% resistance=1k package=THT]
  U2 = SIP - 6 pins [chip_label=LCD package="SIP (Single Inline) [THT]"]
  R2 = Resistor [tolerance=±5% resistance=1.5k package=THT]
  R3 = Resistor [tolerance=±5% resistance=1.5k package=THT]
  U3 = PN532 [chip_label=PN532 package="SIP (Single Inline) [THT]"]

nets:
  N1: Q1.Gate, R1.Pin_0
  N2: Q1.drain, L1.pin1, D1.anode
  GND: Q1.source, Raspberry_Pi_1.GND, U2.GND, U3.GND
  3.3V: Raspberry_Pi_1.3v3, U2.3.3V, R2.Pin_1, R3.Pin_1, U3.3.3V
  N3: Raspberry_Pi_1.GPIO2, U2.Data, R2.Pin_0, U3.MOSI/SDA/TX
  N4: Raspberry_Pi_1.GPIO3, U2.CLK, R3.Pin_0, U3.SSCL/SCL/RX
  N5: Raspberry_Pi_1.GPIO26, R1.Pin_1
  N6: Raspberry_Pi_1.5V, L1.pin2, D1.cathode

custom parts:
  SIP - 6 pins: A SIP stand-in part for whatever you want. With 6 pins on a 300 mil single inline package (SIP) footprint.
  PN532: A SIP stand-in part for whatever you want. With 9 pins on a 300 mil single inline package (SIP) footprint.
